# Fritzing sketch noci_probe (saved by Fritzing 0.9.4)
breadboards: 2

parts:
  C1 = Capacitor [package=cap-pth-small2]  # not connected
  S1 = Pushbutton [package="[SMD]"]
  S2 = Pushbutton [package="[SMD]"]
  S3 = Pushbutton [package="[SMD]"]
  LED1 = smd LED [color="Red (633nm)" package="1206 [SMD]"]
  R1 = Resistor [tolerance=±5% resistance=220 package=THT]
  M1 = volt-ammeter [package=THT]  # not connected

nets:
  N1: S1.Pin_1, S1.Pin_2, S2.Pin_1, S2.Pin_2, S3.Pin_1, S3.Pin_2, LED1.cathode, LED1.anode, R1.Pin_0
  N2: S1.Pin_3, S1.Pin_4
  N3: S2.Pin_3, S2.Pin_4
  N4: S3.Pin_3, S3.Pin_4

notes:
  Microcontroller: D3
  Thermocouple: V+
  PowerSupply: V+
  PowerSupply: GND
  Microcontroler: Pin 11
  Microcontroller: V+
  Microcontroller: GND
  Microcontroller: D9
  Microcontroller: reset
  Microcontroller: A0
  Microcontroller: A1
  Button: ON
  Button: OFF
  Button: RESET
  Microcontroller: SDO
  Microcontroller: SCK
  Microcontroller: 5V
  Microcontroller: SDI
  Thermocouple: GND
  Thermocouple: 3.3
  Thermocouple: CSO
  Thermocouple: SCK
  Thermocouple: SDO
  Thermocouple: SDI
  Thermocouple: DRO
  Thermocouple: DRI
  Thermocouple: CSI
  Microcontroller: D2
  Microcontroller: 3.3
  Microcontroller: M1 -
  Microcontroller: M1 +
  MW Resistor
  MW Probe
  Thick wires
  Thin wires

custom parts:
  volt-ammeter: Volt-ammeter 0-100V 0-10A panel mount.
